// Logisim project Homework2.circ as structural Verilog: 1 circuit, main circuit main
module main (
  input  in_1,
  input  in_2,
  input  in_3,
  input  in_4,
  input  in_5,
  input  in_6,
  input  in_7,
  input  in_8,
  input  in_9,
  input  in_10,
  input  in_11,
  input  in_12,
  output out_13,
  output out_14,
  output out_15
);

  wire or_1_out, or_2_out, or_3_out, or_6_out, or_7_out, or_8_out;

  or or_1 (or_1_out, in_1, in_2);
  or or_2 (or_2_out, in_3, in_4);
  or or_3 (or_3_out, in_9, in_11);
  or or_4 (out_13, or_1_out, or_2_out);
  or or_5 (out_15, or_3_out, in_12);
  or or_6 (or_6_out, in_5, in_6);
  or or_7 (or_7_out, in_7, in_8);
  or or_8 (or_8_out, or_6_out, or_7_out);
  or or_9 (out_14, or_8_out, in_10);

  // Notes on the sheet:
  //   #6
  //   #7
  //   #8
endmodule
