// Logisim project LAB1.circ as structural Verilog: 1 circuit, main circuit main
module main (
  input  X,
  input  Y,
  input  A,
  input  B,
  input  C,
  input  D,
  input  A_2,
  input  B_2,
  input  A_3,
  input  C_2,
  input  B_3,
  input  D_2,
  input  C_3,
  input  E,
  output F,
  output out_16,
  output F_2,
  output F_3
);

  wire and_1_out, and_2_out, and_3_out, and_4_out, and_5_out, and_8_out, and_9_out, and_10_out, not_1_out,
       not_2_out;

  not not_1 (not_1_out, X);
  not not_2 (not_2_out, Y);
  and and_1 (and_1_out, A, B);
  and and_2 (and_2_out, C, D);
  and and_3 (and_3_out, not_1_out, Y);
  and and_4 (and_4_out, X, not_2_out);
  or or_1 (F, and_3_out, and_4_out);
  and and_5 (and_5_out, B_3, C_3);
  and and_6 (out_16, and_1_out, and_2_out);
  and and_7 (F_3, A_3, and_5_out);
  and and_8 (and_8_out, A_2, B_2);
  and and_9 (and_9_out, C_2, D_2);
  and and_10 (and_10_out, and_8_out, and_9_out);
  and and_11 (F_2, and_10_out, E);

  // Notes on the sheet:
  //   First Circuit
  //   #1
  //   XOR
  //   #2
  //   F
  //   #3
endmodule
