// Logisim project HOMEWORK3.circ as structural Verilog: 1 circuit, main circuit main
module main (
  input  A,
  input  A_2,
  input  B,
  input  B_2,
  input  C,
  input  C_2,
  input  A_3,
  input  X,
  input  B_3,
  input  Y,
  input  C_3,
  input  D,
  input  W,
  input  Z,
  input  A_4,
  input  C_4,
  input  B_4,
  output F,
  output F_2,
  output F_3,
  output F_4,
  output F_5
);

  wire and_1_out, and_2_out, and_3_out, and_4_out, and_5_out, and_6_out, not_1_out, not_2_out, not_3_out,
       not_4_out, not_5_out, not_6_out, not_7_out, not_8_out, or_3_out, or_4_out, or_5_out, or_6_out;

  not not_1 (not_1_out, B);
  and and_1 (and_1_out, A, B);
  and and_2 (and_2_out, not_1_out, C_2);
  not not_2 (not_2_out, A_3);
  not not_3 (not_3_out, D);
  not not_4 (not_4_out, B_3);
  not not_5 (not_5_out, C_3);
  or or_1 (F_2, and_1_out, and_2_out);
  and and_3 (and_3_out, A_3, B_3, C_3);
  and and_4 (and_4_out, A_3, B_3, C_3, D);
  and and_5 (and_5_out, not_2_out, not_3_out);
  and and_6 (and_6_out, not_4_out, not_5_out);
  or or_2 (F_4, and_3_out, and_4_out, and_5_out, and_6_out);
  or or_3 (or_3_out, A_4, C_4);
  not not_6 (not_6_out, B_4);
  and and_7 (F_5, or_3_out, A_4, not_6_out);
  or or_4 (or_4_out, A_2, B_2);
  not not_7 (not_7_out, B_2);
  or or_5 (or_5_out, not_7_out, C);
  or or_6 (or_6_out, X, Y);
  not not_8 (not_8_out, W);
  and and_8 (F, or_4_out, or_5_out);
  and and_9 (F_3, or_6_out, not_8_out, Z);

  // Notes on the sheet:
  //   a.
  //   AB
  //   B'C
  //   c.
  //   ABC
  //   ABCD
  //   A'D'
  //   B'C'
  //   e.
  //   A+C
  //   b.
  //   A+B
  //   B'+C
  //   d.
  //   X+Y
endmodule
