// Logisim project LAB3.circ as structural Verilog: 1 circuit, main circuit main
module main (
  input  A,
  input  A_2,
  input  D,
  input  B,
  input  C,
  input  E,
  input  D_2,
  input  E_2,
  input  F,
  input  F_2,
  input  B_2,
  input  C_2,
  input  B_3,
  input  B_4,
  input  C_3,
  input  A_3,
  input  A_4,
  input  C_4,
  output G,
  output Z,
  output F_3,
  output F_4
);

  wire and_1_out, and_2_out, and_4_out, and_5_out, and_6_out, and_7_out, not_1_out, not_2_out, or_1_out,
       or_2_out, or_3_out;

  not not_1 (not_1_out, C_2);
  not not_2 (not_2_out, D);
  or or_1 (or_1_out, B_3, C_3);
  and and_1 (and_1_out, A, not_2_out);
  and and_2 (and_2_out, B_2, not_1_out);
  and and_3 (F_3, or_1_out, A_4);
  or or_2 (or_2_out, and_1_out, E);
  and and_4 (and_4_out, or_2_out, F);
  or or_3 (or_3_out, and_4_out, and_2_out);
  not not_3 (Z, or_3_out);
  and and_5 (and_5_out, B_4, A_3);
  and and_6 (and_6_out, A_3, C_4);
  or or_4 (F_4, and_5_out, and_6_out);
  and and_7 (and_7_out, A_2, B, C, D_2);
  or or_5 (G, and_7_out, E_2, F_2);

  // Notes on the sheet:
  //   3. F
  //   5. F
  //   5. C
endmodule
