// Logisim project HOMEWORK4.circ as structural Verilog: 1 circuit, main circuit main
module main (
  input  A,
  input  B,
  input  C,
  input  A_2,
  input  A_3,
  input  B_2,
  input  B_3,
  input  C_2,
  input  D,
  output F,
  output A_prime_B_prime,
  output out_12,
  output F_2,
  output C_prime_A_prime_D_ABD_prime
);

  wire and_1_out, and_2_out, and_3_out, nand_1_out, nand_3_out, nor_1_out, not_1_out, not_2_out, not_3_out,
       not_4_out, not_5_out, not_6_out, or_1_out;

  not not_1 (not_1_out, D);
  and and_1 (and_1_out, A_2, B_2, not_1_out);
  and and_2 (and_2_out, A, B);
  or or_1 (or_1_out, B, C);
  not not_2 (not_2_out, A);
  not not_3 (not_3_out, B);
  nand nand_1 (nand_1_out, A_2, B_2);
  and and_3 (and_3_out, C_2, D);
  not not_4 (not_4_out, D);
  not not_5 (not_5_out, A_2);
  nor nor_1 (nor_1_out, nand_1_out, and_3_out);
  nand nand_2 (F, and_2_out, or_1_out);
  or or_2 (A_prime_B_prime, not_2_out, not_3_out);
  nand nand_3 (nand_3_out, A_2, C_2, not_4_out);
  not not_6 (not_6_out, C_2);
  or or_3 (F_2, nor_1_out, nand_3_out);
  or or_4 (C_prime_A_prime_D_ABD_prime, not_6_out, not_5_out, and_1_out, D);
  or or_5 (out_12, A_3, B_3);

  // Notes on the sheet:
  //   ABD'
  //   ex 2.1
  //   AB
  //   B+C
  //   ex 2.2
  //   (AB)'
  //   CD
  //   ((AB)(B+C))'
  //   ((AB)'+CD)'
  //   (ACD')'
  //   Fsimp
  //   Fsimp
  //   ex 2.3
endmodule
