// Logisim project LAB4.circ as structural Verilog: 1 circuit, main circuit main
module main (
  input  A,
  input  B,
  input  C,
  input  B_2,
  input  C_2,
  input  A_2,
  input  A_3,
  input  A_4,
  input  B_3,
  input  A_5,
  input  A_6,
  input  A_7,
  input  A_8,
  input  B_4,
  input  B_5,
  input  A_9,
  input  A_10,
  input  B_6,
  input  B_7,
  output F,
  output F_2,
  output G,
  output AB_AC,
  output F_3,
  output F_4,
  output G_2,
  output G_3,
  output F_5,
  output F_6,
  output F_7,
  output F_8,
  output G_4,
  output A_prime_B_prime,
  output F_9,
  output F_10,
  output F_11,
  output G_5
);

  wire and_1_out, and_2_out, and_9_out, and_10_out, and_11_out, and_12_out, and_14_out, and_15_out,
       and_16_out, not_1_out, not_2_out, not_3_out, not_4_out, not_6_out, not_8_out, not_9_out, not_10_out,
       not_12_out, not_13_out, or_1_out, or_4_out;

  not not_1 (not_1_out, A_6);
  and and_1 (and_1_out, B, C);
  and and_2 (and_2_out, B, A_2);
  and and_3 (F_4, A_3, B_3);
  and and_4 (G_3, B_3, A_3);
  and and_5 (F_6, A_6, not_1_out);
  or or_1 (or_1_out, A_7, B_4);
  not not_2 (not_2_out, A_7);
  not not_3 (not_3_out, B_4);
  not not_4 (not_4_out, A_9);
  and and_6 (F_2, and_1_out, A_2);
  and and_7 (G, C, and_2_out);
  not not_5 (F_7, or_1_out);
  and and_8 (A_prime_B_prime, not_2_out, not_3_out);
  and and_9 (and_9_out, not_4_out, B_6);
  or or_2 (F_10, A_9, and_9_out);
  or or_3 (F_11, A_9, B_6);
  not not_6 (not_6_out, A_4);
  and and_10 (and_10_out, A, C_2);
  not not_7 (F_3, not_6_out);
  not not_8 (not_8_out, A_5);
  not not_9 (not_9_out, A_8);
  not not_10 (not_10_out, B_5);
  or or_4 (or_4_out, B_2, C_2);
  and and_11 (and_11_out, A, B_2);
  or or_5 (F_5, A_5, not_8_out);
  not not_11 (F_8, and_12_out);
  and and_12 (and_12_out, A_8, B_5);
  or or_6 (G_4, not_9_out, not_10_out);
  not not_12 (not_12_out, B_7);
  and and_13 (F, A, or_4_out);
  or or_7 (AB_AC, and_11_out, and_10_out);
  and and_14 (and_14_out, A_10, not_12_out);
  and and_15 (and_15_out, B_7, A_10);
  not not_13 (not_13_out, and_14_out);
  not not_14 (G_5, and_15_out);
  not not_15 (F_9, and_16_out);
  and and_16 (and_16_out, A_10, not_13_out);

  assign G_2 = A_4;

  // Notes on the sheet:
  //   EX5
  //   EX1
  //   BC
  //   AB
  //   EX2
  //   AB
  //   BA
  //   EX8
  //   AA'
  //   (A+B)'
  //   A'B
  //   BCA
  //   CAB
  //   G
  //   A+A'B
  //   A+B
  //   EX7
  //   EX3
  //   AC
  //   EX4
  //   Ex6
  //   B+C
  //   AB
  //   A+A'
  //   (AB)'
  //   A'+B'
  //   A(B+C)
  //   EX9
  //   (AB')'
  //   (AB)'
  //   (A(AB')')'
  //   (A(AB')')'
  //   (A(A'+B''))'
  //   A'(A'+B)
  //   A'+A''B'
  //   A'+AB''
endmodule
