// Logisim project HW5.circ as structural Verilog: 1 circuit, main circuit main
module main (
  input  A,
  input  A_2,
  input  A_3,
  input  A_4,
  input  A_5,
  input  C,
  input  B,
  input  B_2,
  input  A_6,
  input  C_2,
  input  B_3,
  input  D,
  input  in_13,
  output A_prime,
  output A_B,
  output AB,
  output out_17,
  output out_18
);

  wire and_1_out, and_2_out, and_3_out, nand_1_out, nand_2_out, nand_3_out, nor_2_out, nor_3_out, nor_5_out,
       not_1_out, not_2_out;

  nor nor_1 (A_prime, A_2, A_2);
  nor nor_2 (nor_2_out, A_4, A_4);
  nor nor_3 (nor_3_out, B, B);
  nor nor_4 (AB, nor_2_out, nor_3_out);
  and and_1 (and_1_out, C_2, C_2);
  nand nand_1 (nand_1_out, A_6, C_2);
  nand nand_2 (nand_2_out, and_1_out, A_6, B_3, D);
  nor nor_5 (nor_5_out, A, A_3);
  not nand_3 (nand_3_out, nand_1_out);  // NAND_Gate
  not not_1 (not_1_out, A_5);
  not not_2 (not_2_out, B_2);
  nand nand_4 (out_18, nand_3_out, nand_3_out);
  nor nor_6 (A_B, nor_5_out, nor_5_out);
  and and_2 (and_2_out, not_1_out, B_2);
  and and_3 (and_3_out, A_5, not_2_out);
  or or_1 (out_17, and_2_out, C, and_3_out);

  // Notes on the sheet:
  //   ex1
  //   ex3
  //   A'
  //   B'
  //   ex7
  //   ex2
  //   pos
  //   ex5
endmodule
