// Logisim project LAB5.circ as structural Verilog: 1 circuit, main circuit main
module main (
  input  A,
  input  A_2,
  input  B,
  input  A_3,
  input  A_4,
  input  B_2,
  input  B_3,
  input  C,
  input  D,
  input  A_5,
  input  B_4,
  input  A_6,
  input  B_5,
  input  C_2,
  input  A_7,
  input  D_2,
  input  B_6,
  input  A_8,
  input  B_7,
  input  A_9,
  input  B_8,
  input  C_3,
  input  D_3,
  output AB,
  output A_prime,
  output A_B,
  output AB_CD,
  output A_B__AB__prime,
  output A_B__C_D,
  output out_30,
  output out_31,
  output out_32
);

  wire and_1_out, and_2_out, and_3_out, and_4_out, and_5_out, and_6_out, nand_1_out, nand_2_out, nand_5_out,
       nand_6_out, nand_7_out, nand_8_out, nand_9_out, nand_10_out, nand_11_out, nor_1_out, nor_2_out,
       not_1_out, not_2_out, not_3_out, not_4_out, not_5_out, not_6_out, not_7_out, or_2_out;

  nand nand_1 (nand_1_out, A_3, A_3);
  nand nand_2 (nand_2_out, B_3, B_3);
  nand nand_3 (A_prime, A_2, A_2);
  nor nor_1 (nor_1_out, A_6, B_5);
  nor nor_2 (nor_2_out, C_2, D_2);
  nand nand_4 (A_B, nand_1_out, nand_2_out);
  nor nor_3 (A_B__C_D, nor_1_out, nor_2_out);
  nand nand_5 (nand_5_out, A_8, A_8);
  nand nand_6 (nand_6_out, B_7, B_7);
  not not_1 (not_1_out, A_9);
  not not_2 (not_2_out, B_8);
  not not_3 (not_3_out, C_3);
  not not_4 (not_4_out, D_3);
  nand nand_7 (nand_7_out, nand_5_out, B_7);
  nand nand_8 (nand_8_out, A_8, nand_6_out);
  and and_1 (and_1_out, not_1_out, not_2_out, C_3, D_3);
  and and_2 (and_2_out, not_1_out, B_8, not_3_out, not_4_out);
  and and_3 (and_3_out, A_9, not_2_out, not_4_out);
  nand nand_9 (nand_9_out, A, B);
  nand nand_10 (nand_10_out, A_4, B_2);
  nand nand_11 (nand_11_out, C, D);
  nand nand_12 (out_31, nand_7_out, nand_8_out);
  or or_1 (out_32, and_1_out, and_2_out, and_3_out);
  nand nand_13 (AB, nand_9_out, nand_9_out);
  or or_2 (or_2_out, A_5, B_4);
  and and_4 (and_4_out, A_5, B_4);
  not not_5 (not_5_out, A_7);
  not not_6 (not_6_out, B_6);
  nand nand_14 (AB_CD, nand_10_out, nand_11_out);
  not not_7 (not_7_out, and_4_out);
  and and_5 (and_5_out, not_5_out, B_6);
  and and_6 (and_6_out, A_7, not_6_out);
  and and_7 (A_B__AB__prime, or_2_out, not_7_out);
  or or_3 (out_30, and_5_out, and_6_out);

  // Notes on the sheet:
  //   Ex1
  //   Ex3
  //   Ex5
  //   Ex7
  //   Ex8
  //   A'B'CD
  //   A'BC'D'
  //   AB'D'
  //   Ex2
  //   (AB)'
  //   (CD)'
  //   Ex4
  //   Ex6
endmodule
